// Logisim project procesor.circ as structural Verilog
module Procesor (
  input  [7:0] Adress,
  input  [7:0] in_2,
  input  LD,
  input  [7:0] in_4,
  input  [7:0] in_5,
  input  in_6,
  input  [3:0] in_7,
  input  [2:0] SRC,
  input  [2:0] DEST,
  output [7:0] out_10,
  output [7:0] out_11,
  output [7:0] out_12,
  output out_13
);

  wire clock_1_out, clock_2_out;

  Clock clock_1 (.out(clock_1_out));
  RAM #(.bus("separate")) ram_1 (
    .addr(Adress), .din(in_2), .data(out_10), .clk(clock_1_out), .ld(LD));  // open: str, sel, clr
  ALU alu_1 (
    .R1__Value_of_first_register(in_4), .R2__Value_of_second_register(in_5), .OUT__ALU_output(out_11),
    .FL__output_to_FLAG(out_13), .COM__Value_of_command__0000_to_1111(in_7));
  Clock clock_2 (.out(clock_2_out));
  Registers registers_1 (
    .DESTINATION(DEST), .VALUE1(out_12), .CLK(clock_2_out), .SOURCE1(SRC), .in_6(in_6), .MEM(out_11));  // open: VALUE2, SOURCE2, AX
endmodule
